# Fritzing sketch sketch (saved by Fritzing 0.9.3b)
perfboards: 1

parts:
  Part1 = Arduino Nano (Rev3.0) (ICSP)
  S2 = Pushbutton [package="[THT]"]
  S3 = Pushbutton [package="[THT]"]
  S4 = Pushbutton [package="[THT]"]
  S5 = Pushbutton [package="[THT]"]
  Part2 = Triple Axis Accelerometer Breakout - ADXL335
  NEOPIXEL3 = Neopixel Strip -- White (60/m)
  NEOPIXEL4 = Neopixel Strip -- White (60/m)
  VCC1 = 4 x AAA Battery Mount
  VCC2 = 4 x AAA Battery Mount  # not connected
  S6 = Toggle Switch [package=THT]
  S7 = Toggle Switch [package=THT]

nets:
  GND: Part1.GND, Part2.GND, VCC1.-
  N1: Part1.D2, NEOPIXEL4.+5V
  N2: Part1.D4, NEOPIXEL3.+5V
  N3: Part1.D6, S2.Pin_3, S2.Pin_4
  N4: Part1.D7, S3.Pin_3, S3.Pin_4
  N5: Part1.D8, S4.Pin_4
  N6: Part1.D10, S5.Pin_4
  N7: Part1.A4, Part2.ZOUT
  N8: Part1.A2, Part2.YOUT
  N9: Part1.A0, Part2.XOUT
  GND_2: NEOPIXEL3.GND, NEOPIXEL4.GND
  N10: NEOPIXEL4.DI, S7.COM
  N11: NEOPIXEL4.DO, S6.COM

custom parts:
  Neopixel Strip -- White (60/m): Neopixel Strip, White, 60 pixels per meter.
